# Fritzing sketch simon (saved by Fritzing 0.9.2b)
breadboards: 1

parts:
  Part2 = Arduino Uno (Rev3)
  J1 = Piezo Speaker
  LED2 = smd LED [color="Orange (620nm)" package="0603 [SMD]"]
  LED3 = smd LED [color="Green (570nm)" package="0603 [SMD]"]
  LED4 = smd LED [color="Red (633nm)" package="0603 [SMD]"]
  S1 = Pushbutton [package="[SMD]"]
  S2 = Pushbutton [package="[SMD]"]
  S3 = Pushbutton [package="[SMD]"]

nets:
  N1: Part2.D8, LED2.anode
  N2: Part2.D9_PWM, LED3.anode
  N3: Part2.D10_PWM/SS, LED4.anode
  N4: Part2.D11_PWM/MOSI, J1.pin2
  N5: Part2.D2, S1.Pin_1, S1.Pin_2
  N6: Part2.D4, S2.Pin_1, S2.Pin_2
  N7: Part2.D6_PWM, S3.Pin_1, S3.Pin_2
  N8: Part2.GND, J1.pin1, LED2.cathode, LED3.cathode, LED4.cathode, S1.Pin_3, S1.Pin_4, S2.Pin_3, S2.Pin_4, S3.Pin_3, S3.Pin_4
