# Fritzing sketch photoresistor_nopcb_ethernet (saved by Fritzing 0.9.2b)
breadboards: 1

parts:
  R2 = Resistor [tolerance=±5% resistance=220 package=THT]
  R1 = PHOTOCELL [package=photocell-kit]
  Part1 = Arduino Ethernet Shield (Rev3)

nets:
  N1: R2.Pin_0, R1.P$1, Part1.A0
  N2: R2.Pin_1, Part1.5V
  N3: R1.P$2, Part1.GND
